// Logisim project TrafficLight.circ as structural Verilog: 9 circuits, main circuit main
module main (
);

  wire clock_1_out, dipswitch_1_p1, dipswitch_1_p2, mode_store_1_emergency_out, mode_store_1_night_out,
       n7_segment_display_1_p1, n7_segment_display_2_p1, n7_segment_display_3_p1, n7_segment_display_4_p1,
       state_tramsform_1_ewgreen, state_tramsform_1_ewred, state_tramsform_1_ewyellow,
       state_tramsform_1_nsgreen, state_tramsform_1_nsred, state_tramsform_1_nsyellow, timing_module_1_timeup;
  wire [1:0] sit_module_1_state;
  wire [2:0] EW_red_out, NS_red_out;
  wire [5:0] EWtime_timeout, EWtiming_resttime, NStime_timeout, NStiming_resttime;

  Clock clock_1 (.out(clock_1_out));
  sit_module sit_module_1 (.cp(clock_1_out), .TimeUp(timing_module_1_timeup), .State(sit_module_1_state));
  timing_module timing_module_1 (
    .T00(6'b100011), .T01(6'b000101), .T10(6'b100011), .T11(6'b000101), .cp(clock_1_out),
    .State(sit_module_1_state), .TimeUp(timing_module_1_timeup));  // open: restTime
  // DipSwitch #(.number(2)) dipswitch_1: pin names not known; wires that end beside it: dipswitch_1_p1, dipswitch_1_p2
  state_tramsform state_tramsform_1 (
    .in_1(sit_module_1_state), .EWRed(state_tramsform_1_ewred), .EWYellow(state_tramsform_1_ewyellow),
    .EWGreen(state_tramsform_1_ewgreen), .NSRed(state_tramsform_1_nsred),
    .NSYellow(state_tramsform_1_nsyellow), .NSGreen(state_tramsform_1_nsgreen));
  mode_store mode_store_1 (
    .Emergency_in(dipswitch_1_p1), .Night_in(dipswitch_1_p2), .cp(clock_1_out),
    .Emergency_out(mode_store_1_emergency_out), .Night_out(mode_store_1_night_out));
  timing_module NStiming (
    .T00(6'b101000), .T01(6'b000101), .T10(6'b100011), .T11(6'b000101), .cp(clock_1_out),
    .State(sit_module_1_state), .restTime(NStiming_resttime));  // open: TimeUp
  timing_module EWtiming (
    .T00(6'b100011), .T01(6'b000101), .T10(6'b101000), .T11(6'b000101), .cp(clock_1_out),
    .State(sit_module_1_state), .restTime(EWtiming_resttime));  // open: TimeUp
  timing_control NStime (
    .time_in(NStiming_resttime), .Emergency(mode_store_1_emergency_out), .Night(mode_store_1_night_out),
    .timeout(NStime_timeout));
  timing_control EWtime (
    .time_in(EWtiming_resttime), .Emergency(mode_store_1_emergency_out), .Night(mode_store_1_night_out),
    .timeout(EWtime_timeout));
  light_control EW (
    .red_on(state_tramsform_1_ewred), .yellow_on(state_tramsform_1_ewyellow),
    .green_on(state_tramsform_1_ewgreen), .energency(mode_store_1_emergency_out),
    .night(mode_store_1_night_out), .cp(clock_1_out), .red_out(EW_red_out[0]), .yellow_out(EW_red_out[1]),
    .green_out(EW_red_out[2]));
  light_control NS (
    .red_on(state_tramsform_1_nsred), .yellow_on(state_tramsform_1_nsyellow),
    .green_on(state_tramsform_1_nsgreen), .energency(mode_store_1_emergency_out),
    .night(mode_store_1_night_out), .cp(clock_1_out), .red_out(NS_red_out[0]), .yellow_out(NS_red_out[1]),
    .green_out(NS_red_out[2]));
  LED led_1 (.in(EW_red_out[0]));
  LED led_2 (.in(EW_red_out[1]));
  LED led_3 (.in(EW_red_out[2]));
  // _7_Segment_Display 7_segment_display_1: pin names not known; wires that end beside it: n7_segment_display_1_p1, n7_segment_display_1_p1
  // _7_Segment_Display 7_segment_display_2: pin names not known; wires that end beside it: n7_segment_display_2_p1, n7_segment_display_2_p1
  // BCD_to_7_Segment_decoder bcd_to_7_segment_decoder_1: pin names not known
  // BCD_to_7_Segment_decoder bcd_to_7_segment_decoder_2: pin names not known
  // Binary_to_BCD_converter #(.binvalue(6)) binary_to_bcd_converter_1: pin names not known; wires that end beside it: EWtime_timeout
  LED led_4 (.in(NS_red_out[0]));
  LED led_5 (.in(NS_red_out[1]));
  LED led_6 (.in(NS_red_out[2]));
  // _7_Segment_Display 7_segment_display_3: pin names not known; wires that end beside it: n7_segment_display_3_p1, n7_segment_display_3_p1
  // BCD_to_7_Segment_decoder bcd_to_7_segment_decoder_3: pin names not known
  // Binary_to_BCD_converter #(.binvalue(6)) binary_to_bcd_converter_2: pin names not known; wires that end beside it: NStime_timeout
  // _7_Segment_Display 7_segment_display_4: pin names not known; wires that end beside it: n7_segment_display_4_p1, n7_segment_display_4_p1
  // BCD_to_7_Segment_decoder bcd_to_7_segment_decoder_4: pin names not known

  // Notes on the sheet:
  //   Emergency
  //   Night
  //   EW_Light
  //   NS_Light
endmodule

module sit_module (
  input  cp,
  input  TimeUp,
  output [1:0] State
);

  wire and_1_out, por_1_out, Q0_q, Q0_qn, Q1_q, xor_1_out;

  POR #(.porTransition(2)) por_1 (.out(por_1_out));
  and and_1 (and_1_out, TimeUp, por_1_out);
  xor xor_1 (xor_1_out, Q1_q, Q0_q);
  Multiplexer multiplexer_1 (.in0(Q1_q), .in1(xor_1_out), .out(State[1]), .sel(and_1_out));
  Multiplexer multiplexer_2 (.in0(Q0_q), .in1(Q0_qn), .out(State[0]), .sel(and_1_out));
  D_Flip_Flop Q1 (.D(State[1]), .clk(cp), .Q(Q1_q));  // open: Qn, preset, reset
  D_Flip_Flop Q0 (.D(State[0]), .clk(cp), .Q(Q0_q), .Qn(Q0_qn));  // open: preset, reset
endmodule

module timing_module (
  input  [5:0] T00,
  input  [5:0] T01,
  input  [5:0] T10,
  input  [5:0] T11,
  input  cp,
  input  [1:0] State,
  output [5:0] restTime,
  output TimeUp
);

  wire [5:0] adder_6_bit_1_out_3, multiplexer_1_out, multiplexer_2_out;

  Multiplexer #(.select(2), .width(6)) multiplexer_1 (
    .in0(T00), .in1(T01), .in2(T10), .in3(T11), .out(multiplexer_1_out), .sel(State));
  Multiplexer #(.width(6)) multiplexer_2 (
    .in0(restTime), .in1(multiplexer_1_out), .out(multiplexer_2_out), .sel(TimeUp));
  adder_6_bit adder_6_bit_1 (.in_1(multiplexer_2_out), .in_2({6{1'b1}}), .out_3(adder_6_bit_1_out_3));
  D_Flip_Flop d_ff_1 (.D(adder_6_bit_1_out_3[0]), .clk(cp), .Q(restTime[0]));  // open: Qn, preset, reset
  D_Flip_Flop d_ff_2 (.D(adder_6_bit_1_out_3[1]), .clk(cp), .Q(restTime[1]));  // open: Qn, preset, reset
  D_Flip_Flop d_ff_3 (.D(adder_6_bit_1_out_3[2]), .clk(cp), .Q(restTime[2]));  // open: Qn, preset, reset
  D_Flip_Flop d_ff_4 (.D(adder_6_bit_1_out_3[3]), .clk(cp), .Q(restTime[3]));  // open: Qn, preset, reset
  D_Flip_Flop d_ff_5 (.D(adder_6_bit_1_out_3[4]), .clk(cp), .Q(restTime[4]));  // open: Qn, preset, reset
  D_Flip_Flop d_ff_6 (.D(adder_6_bit_1_out_3[5]), .clk(cp), .Q(restTime[5]));  // open: Qn, preset, reset
  Comparator #(.width(6)) comparator_1 (.a(restTime), .b({6{1'b0}}), .eq(TimeUp));  // open: gt, lt
endmodule

module add (
  input  Ai,
  input  Bi,
  input  Cin,
  output Si,
  output Ci
);

  wire and_1_out, and_2_out, and_3_out;

  xor xor_1 (Si, Ai, Bi, Cin);
  and and_1 (and_1_out, Ai, Bi);
  and and_2 (and_2_out, Cin, Ai);
  and and_3 (and_3_out, Bi, Cin);
  or or_1 (Ci, and_1_out, and_2_out, and_3_out);
endmodule

module adder_6_bit (
  input  [5:0] in_1,
  input  [5:0] in_2,
  output [5:0] out_3
);

  wire add_1_ci, add_2_ci, add_3_ci, add_4_ci, add_5_ci;

  add add_1 (.Ai(in_1[0]), .Bi(in_2[0]), .Cin(1'b0), .Si(out_3[0]), .Ci(add_1_ci));
  add add_2 (.Ai(in_1[1]), .Bi(in_2[1]), .Cin(add_1_ci), .Si(out_3[1]), .Ci(add_2_ci));
  add add_3 (.Ai(in_1[2]), .Bi(in_2[2]), .Cin(add_2_ci), .Si(out_3[2]), .Ci(add_3_ci));
  add add_4 (.Ai(in_1[3]), .Bi(in_2[3]), .Cin(add_3_ci), .Si(out_3[3]), .Ci(add_4_ci));
  add add_5 (.Ai(in_1[4]), .Bi(in_2[4]), .Cin(add_4_ci), .Si(out_3[4]), .Ci(add_5_ci));
  add add_6 (.Ai(in_1[5]), .Bi(in_2[5]), .Cin(add_5_ci), .Si(out_3[5]));  // open: Ci
endmodule

module state_tramsform (
  input  [1:0] in_1,
  output EWRed,
  output EWYellow,
  output EWGreen,
  output NSRed,
  output NSYellow,
  output NSGreen
);

  wire not_1_out, not_2_out;

  not not_1 (not_1_out, in_1[1]);
  not not_2 (not_2_out, in_1[0]);
  and and_1 (EWGreen, not_1_out, not_2_out);
  and and_2 (EWYellow, not_1_out, in_1[0]);
  and and_3 (NSGreen, in_1[1], not_2_out);
  and and_4 (NSYellow, in_1[1], in_1[0]);
  or or_1 (EWRed, NSYellow, NSGreen);
  or or_2 (NSRed, EWYellow, EWGreen);
endmodule

module light_control (
  input  red_on,
  input  yellow_on,
  input  green_on,
  input  energency,
  input  night,
  input  cp,
  output red_out,
  output yellow_out,
  output green_out
);

  wire and_1_out, multiplexer_1_out, not_1_out, or_1_out, or_2_out;

  or or_1 (or_1_out, yellow_on, night);
  not not_1 (not_1_out, energency);
  and and_1 (and_1_out, or_1_out, not_1_out);
  or or_2 (or_2_out, energency, night);
  Multiplexer multiplexer_1 (.in0(red_on), .in1(1'b0), .out(multiplexer_1_out), .sel(or_2_out));
  Multiplexer multiplexer_2 (.in0(1'b0), .in1(cp), .out(yellow_out), .sel(and_1_out));
  Multiplexer multiplexer_3 (.in0(green_on), .in1(1'b0), .out(green_out), .sel(or_2_out));
  or or_3 (red_out, multiplexer_1_out, energency);
endmodule

module mode_store (
  input  Emergency_in,
  input  Night_in,
  input  cp,
  output Emergency_out,
  output Night_out
);

  D_Flip_Flop d_ff_1 (.D(Emergency_in), .clk(cp), .Q(Emergency_out));  // open: Qn, preset, reset
  D_Flip_Flop d_ff_2 (.D(Night_in), .clk(cp), .Q(Night_out));  // open: Qn, preset, reset
endmodule

module timing_control (
  input  [5:0] time_in,
  input  Emergency,
  input  Night,
  output [5:0] timeout
);

  wire or_1_out;
  wire [5:0] undriven;

  or or_1 (or_1_out, Emergency, Night);
  Multiplexer #(.width(6)) multiplexer_1 (.in0(time_in), .in1(undriven), .out(timeout), .sel(or_1_out));
endmodule
